// Logisim project flip flop 03.circ as structural Verilog: 1 circuit, main circuit main
module main (
);

  wire clock_1_out, decodificador_1_p3, decodificador_1_p4, decodificador_1_p5, decodificador_1_p6,
       decodificador_1_p7, decodificador_1_p8, decodificador_1_p9, main_1_p3, main_1_p4;

  Clock clock_1 (.out(clock_1_out));
  // contador_main main_1: pin names not known; wires that end beside it: clock_1_out, clock_1_out, main_1_p3, main_1_p4, main_1_p3, main_1_p4
  // decodificador decodificador_1: pin names not known; wires that end beside it: 1'b0, 1'b0, decodificador_1_p3, decodificador_1_p4, decodificador_1_p5, decodificador_1_p6, decodificador_1_p7, decodificador_1_p8, decodificador_1_p9
  _7_Segment_Display u_7_segment_display_1 (
    .g(decodificador_1_p9), .f(decodificador_1_p8), .a(decodificador_1_p3), .b(decodificador_1_p4),
    .e(decodificador_1_p7), .d(decodificador_1_p6), .c(decodificador_1_p5));  // open: dp
endmodule
